// Logisim project pipelined.circ as structural Verilog: 7 circuits, main circuit main
module Control (
  input  [5:0] Instruction,
  output [1:0] BranchOp,
  output RegDst,
  output SignedIMM,
  output ALUSrc,
  output MemToReg,
  output MemWrite,
  output MemRead,
  output RegWrite,
  output [1:0] AluOp
);

  PLA #(.in_width(6), .out_width(11), .truth_table("000000,10100000100#R-format\n000100,01000000001#beq\n000101,01000000011#bne\n001001,11100010000#addiu\n001010,11100011000#slti\n001100,11100010000#andi\n001101,11100010000#ori\n100011,00110111000#lw\n101011,00001011000#sw")) pla_1 ();  // open: in, out
endmodule

module ALU_control (
  input  [1:0] ALUop,
  input  [2:0] IMM_OP,
  input  [5:0] Funct,
  output [3:0] Output
);

  // PLA #(.in_width(11), .out_width(4), .truth_table("00xxxxxxxxx,0010#lw/sw\n01xxxxxxxxx,0110#beq/bne\n10xxx100001,0010#addu\n10xxx100011,0110#subu\n10xxx100100,0000#AND\n10xxx100101,0001#OR\n10xxx100111,1100#nor\n10xxx101010,0111#slt\n11001xxxxxx,0010#addui\n11010xxxxxx,0111#slti\n11100xxxxxx,0000#andi\n11101xxxxxx,0001#ori")) pla_1: pin names not known; wires that end beside it: Output
endmodule

module Bit_extender (
  input  [15:0] Input,
  input  Signed,
  output [31:0] Output
);

  wire and_1_out;

  Multiplexer #(.width(16)) multiplexer_1 (.in0({16{1'b0}}), .in1({16{1'b1}}), .out(Output[31:16]), .sel(and_1_out));
  and and_1 (and_1_out, Input[15], Signed);

  assign Output[15:0] = Input;
endmodule

module main (
);

  wire alu_control_1_p4, clock_1_out, control_1_alusrc, control_1_memread, control_1_memtoreg,
       control_1_memwrite, control_1_regdst, control_1_signedimm, mips_alu_1_p3, mipsprogramrom_1_p5,
       registerfile_1_p5;
  wire [1:0] control_1_aluop, control_1_branchop;
  wire [4:0] multiplexer_1_out;
  wire [15:0] mipsprogramrom_1_p2, mipsprogramrom_1_p2_2;
  wire [31:0] bit_extender_1_output, branch_control_1_addressout, mips_alu_1_p4, mips_ram_1_p6,
       mipsprogramrom_1_p3, register_1_q, registerfile_1_p6, registerfile_1_p7;

  Branch_Control branch_control_1 (
    .AddressOut(branch_control_1_addressout), .AddressIn(register_1_q), .Zero(mips_alu_1_p3),
    .BranchOp(control_1_branchop), .Difference(mipsprogramrom_1_p2));
  Register #(.width(32)) register_1 (
    .D(branch_control_1_addressout), .en(1'b1), .Q(register_1_q), .clk(clock_1_out));  // open: clr
  Clock clock_1 (.out(clock_1_out));
  // MIPSProgramROM mipsprogramrom_1: pin names not known; wires that end beside it: register_1_q, {mipsprogramrom_1_p2_2, mipsprogramrom_1_p2}, mipsprogramrom_1_p3, clock_1_out, mipsprogramrom_1_p5
  Control control_1 (
    .Instruction(mipsprogramrom_1_p2_2[15:10]), .BranchOp(control_1_branchop), .RegDst(control_1_regdst),
    .SignedIMM(control_1_signedimm), .ALUSrc(control_1_alusrc), .MemToReg(control_1_memtoreg),
    .MemWrite(control_1_memwrite), .MemRead(control_1_memread), .RegWrite(mipsprogramrom_1_p5),
    .AluOp(control_1_aluop));
  Multiplexer #(.width(5)) multiplexer_1 (
    .in0(mipsprogramrom_1_p2_2[4:0]), .in1(mipsprogramrom_1_p2[15:11]), .out(multiplexer_1_out),
    .sel(control_1_regdst));
  // RegisterFile registerfile_1: pin names not known; wires that end beside it: multiplexer_1_out, mipsprogramrom_1_p2_2[4:0], mipsprogramrom_1_p2_2[9:5], mipsprogramrom_1_p2_2[4:0], registerfile_1_p5, registerfile_1_p6, registerfile_1_p7
  Bit_extender bit_extender_1 (
    .Input(mipsprogramrom_1_p2), .Signed(control_1_signedimm), .Output(bit_extender_1_output));
  // ALU_control alu_control_1: pin names not known; wires that end beside it: control_1_aluop, mipsprogramrom_1_p2_2[12:10], mipsprogramrom_1_p2[5:0], alu_control_1_p4
  // Mips_ALU mips_alu_1: pin names not known; wires that end beside it: registerfile_1_p5, alu_control_1_p4, mips_alu_1_p3, mips_alu_1_p4
  Multiplexer #(.width(32)) multiplexer_2 (
    .in0(registerfile_1_p6), .in1(bit_extender_1_output), .out(registerfile_1_p7), .sel(control_1_alusrc));
  Multiplexer #(.width(32)) multiplexer_3 (
    .in0(mips_alu_1_p4), .in1(mips_ram_1_p6), .out(mipsprogramrom_1_p3), .sel(control_1_memtoreg));
  // MIPS_RAM #(.addrWidth(24)) mips_ram_1: pin names not known; wires that end beside it: mips_alu_1_p4[23:0], registerfile_1_p6, control_1_memwrite, control_1_memread, clock_1_out, mips_ram_1_p6

  // Notes on the sheet:
  //   contents of mipsprogramrom_1 (hex, n*v repeats v):
  //   addiu $1, $1, 0x1      # $1 = 0x0001     addiu $2, $2, 0x2      # $2 = 0x0002     slt $3, $1, $2
  //   # $3 = 1     slt $3, $2, $1         # $3 = 0     slti $3, $1, 0x1       # $3 = 1     slti $3, $1,
  //   0x42      # $3 = 0     or $3, $1, $2          # $3 = 0x3     and $3, $1, $2         # $3 = 0     ori
  //   $3, $1, 0x7        # $3 = 0x7     andi $3, $1, 0x7       # $3 = 0x1     sw $3, 0($0)     lw $5,
  //   0($0)     beq $1, $3, LOL
endmodule

module Branch_Control (
  input  Zero,
  input  [1:0] BranchOp,
  input  [31:0] AddressIn,
  input  [15:0] Difference,
  output [31:0] AddressOut
);

  wire and_1_out, xor_1_out;
  wire [31:0] adder_1_out, adder_2_out, bit_extender_1_output, shifter_1_out;

  Adder #(.width(32)) adder_1 (.a(AddressIn), .b(32'h4), .out(adder_1_out));  // open: cin, cout
  Multiplexer #(.width(32)) multiplexer_1 (.in0(adder_1_out), .in1(adder_2_out), .out(AddressOut), .sel(and_1_out));
  and and_1 (and_1_out, xor_1_out, BranchOp[0]);
  xor xor_1 (xor_1_out, Zero, BranchOp[1]);
  Bit_extender bit_extender_1 (.Input(Difference), .Signed(1'b1), .Output(bit_extender_1_output));
  Shifter #(.width(32)) shifter_1 (.in(bit_extender_1_output), .\dist (5'b00010), .out(shifter_1_out));
  Adder #(.width(32)) adder_2 (.a(adder_1_out), .b(shifter_1_out), .out(adder_2_out));  // open: cin, cout
endmodule

module main2 (
);

  wire clock_1_out, control2_1_signedimm, EX_MEM_Memory_2_q, EX_MEM_RegisterWriting_q, mips_alu_1_p4,
       mipsprogramrom_1_p3, mipsprogramrom_1_p6;
  wire [1:0] control2_1_branching, control2_1_registerwriting, ID_EX_Branching_q, ID_EX_RegisterWriting_q,
       mips_alu_1_p6;
  wire [2:0] control2_1_alu, control2_1_memory, EX_MEM_Memory_q, ID_EX_Alu_q, ID_EX_Memory_q;
  wire [3:0] mips_alu_1_p3;
  wire [4:0] EX_MEM_RegDst_q, mipsprogramrom_1_p7, multiplexer_3_out;
  wire [31:0] adder_1_out, adder_2_out, bit_extender_1_output, EX_MEM_Result_2_q, EX_MEM_Result_q,
       ID_EX_IMM_q, ID_EX_OP_q, ID_EX_PC_q, ID_EX_rd_q, ID_EX_rs_q, ID_EX_WriteData_q, IF_ID_OP_q,
       IF_ID_PC_q, mips_alu_1_p2, mips_alu_1_p5, mips_ram_1_p6, mipsprogramrom_1_p1, mipsprogramrom_1_p2,
       mipsprogramrom_1_p4, multiplexer_1_out, PC_q, registerfile_1_p1, registerfile_1_p4, registerfile_1_p5,
       shifter_1_out;

  Adder #(.width(32)) adder_1 (.a(32'h4), .b(mipsprogramrom_1_p1), .out(adder_1_out));  // open: cin, cout
  Multiplexer #(.width(32)) multiplexer_1 (
    .in0(mipsprogramrom_1_p2), .in1(adder_1_out), .out(multiplexer_1_out), .sel(mipsprogramrom_1_p3));
  Clock clock_1 (.out(clock_1_out));
  Register #(.width(32)) PC (.D(multiplexer_1_out), .en(1'b1), .Q(PC_q), .clk(clock_1_out));  // open: clr
  // MIPSProgramROM mipsprogramrom_1: pin names not known; wires that end beside it: mipsprogramrom_1_p1, mipsprogramrom_1_p2, mipsprogramrom_1_p3, mipsprogramrom_1_p4, clock_1_out, mipsprogramrom_1_p6, mipsprogramrom_1_p7
  Register #(.width(32)) IF_ID_PC (.D(PC_q), .en(1'b1), .Q(IF_ID_PC_q), .clk(clock_1_out));  // open: clr
  Register #(.width(32)) IF_ID_OP (.D(mipsprogramrom_1_p4), .en(1'b1), .Q(IF_ID_OP_q), .clk(clock_1_out));  // open: clr
  // RegisterFile registerfile_1: pin names not known; wires that end beside it: registerfile_1_p1, IF_ID_OP_q[25:21], IF_ID_OP_q[20:16], registerfile_1_p4, registerfile_1_p5
  Bit_extender bit_extender_1 (.Input(IF_ID_OP_q[15:0]), .Signed(control2_1_signedimm), .Output(bit_extender_1_output));
  Control2 control2_1 (
    .Instruction(IF_ID_OP_q[31:26]), .SignedIMM(control2_1_signedimm), .Alu(control2_1_alu),
    .Branching(control2_1_branching), .Memory(control2_1_memory), .RegisterWriting(control2_1_registerwriting));
  Register #(.width(32)) ID_EX_PC (.D(IF_ID_PC_q), .en(1'b1), .Q(ID_EX_PC_q), .clk(clock_1_out));  // open: clr
  Register #(.width(32)) ID_EX_rd (.D(registerfile_1_p4), .en(1'b1), .Q(ID_EX_rd_q), .clk(clock_1_out));  // open: clr
  Register #(.width(32)) ID_EX_rs (.D(registerfile_1_p5), .en(1'b1), .Q(ID_EX_rs_q), .clk(clock_1_out));  // open: clr
  Register #(.width(32)) ID_EX_IMM (
    .D(bit_extender_1_output), .en(1'b1), .Q(ID_EX_IMM_q), .clk(clock_1_out));  // open: clr
  Register #(.width(3)) ID_EX_Alu (.D(control2_1_alu), .en(1'b1), .Q(ID_EX_Alu_q), .clk(clock_1_out));  // open: clr
  Register #(.width(2)) ID_EX_Branching (
    .D(control2_1_branching), .en(1'b1), .Q(ID_EX_Branching_q), .clk(clock_1_out));  // open: clr
  Register #(.width(32)) ID_EX_OP (.D(IF_ID_OP_q), .en(1'b1), .Q(ID_EX_OP_q), .clk(clock_1_out));  // open: clr
  Register #(.width(3)) ID_EX_Memory (
    .D(control2_1_memory), .en(1'b1), .Q(ID_EX_Memory_q), .clk(clock_1_out));  // open: clr
  Register #(.width(2)) ID_EX_RegisterWriting (
    .D(control2_1_registerwriting), .en(1'b1), .Q(ID_EX_RegisterWriting_q), .clk(clock_1_out));  // open: clr
  Shifter #(.width(32)) shifter_1 (.in(ID_EX_IMM_q), .\dist (5'b00010), .out(shifter_1_out));
  // Mips_ALU mips_alu_1: pin names not known; wires that end beside it: ID_EX_rd_q, mips_alu_1_p2, mips_alu_1_p3, mips_alu_1_p4, mips_alu_1_p5, mips_alu_1_p6
  Multiplexer #(.width(32)) multiplexer_2 (
    .in0(ID_EX_IMM_q), .in1(ID_EX_rs_q), .out(mips_alu_1_p2), .sel(ID_EX_Alu_q[0]));
  Adder #(.width(32)) adder_2 (.a(ID_EX_PC_q), .b(shifter_1_out), .out(adder_2_out));  // open: cin, cout
  ALU_control alu_control_1 (
    .ALUop(ID_EX_Alu_q[2:1]), .Output(mips_alu_1_p3), .Funct(ID_EX_OP_q[5:0]), .IMM_OP(ID_EX_OP_q[28:26]));
  Multiplexer #(.width(5)) multiplexer_3 (
    .in0(ID_EX_OP_q[20:16]), .in1(ID_EX_OP_q[15:11]), .out(multiplexer_3_out),
    .sel(ID_EX_RegisterWriting_q[0]));
  Register #(.width(32)) EX_MEM_BranchPC (.D(adder_2_out), .en(1'b1), .clk(clock_1_out));  // open: Q, clr
  Register #(.width(1)) EX_MEM_Zero (.D(mips_alu_1_p4), .en(1'b1), .clk(clock_1_out));  // open: Q, clr
  Register #(.width(32)) EX_MEM_Result (
    .D(mips_alu_1_p5), .en(1'b1), .Q(EX_MEM_Result_q), .clk(clock_1_out));  // open: clr
  Register #(.width(32)) ID_EX_WriteData (
    .D(ID_EX_rs_q), .en(1'b1), .Q(ID_EX_WriteData_q), .clk(clock_1_out));  // open: clr
  Register #(.width(2)) EX_MEM_Branching (
    .D(ID_EX_Branching_q), .en(1'b1), .Q(mips_alu_1_p6), .clk(clock_1_out));  // open: clr
  Register #(.width(5)) EX_MEM_RegDst (
    .D(multiplexer_3_out), .en(1'b1), .Q(EX_MEM_RegDst_q), .clk(clock_1_out));  // open: clr
  Register #(.width(3)) EX_MEM_Memory (
    .D(ID_EX_Memory_q), .en(1'b1), .Q(EX_MEM_Memory_q), .clr(clock_1_out));  // open: clk
  Register #(.width(1)) EX_MEM_RegisterWriting (
    .D(ID_EX_RegisterWriting_q[1]), .en(1'b1), .Q(EX_MEM_RegisterWriting_q), .clk(clock_1_out));  // open: clr
  // MIPS_RAM #(.addrWidth(24)) mips_ram_1: pin names not known; wires that end beside it: EX_MEM_Result_q[23:0], ID_EX_WriteData_q, EX_MEM_Memory_q[1], EX_MEM_Memory_q[0], clock_1_out, mips_ram_1_p6
  Register #(.width(32)) EX_MEM_Result_2 (
    .D(EX_MEM_Result_q), .en(1'b1), .Q(EX_MEM_Result_2_q), .clk(clock_1_out));  // open: clr
  Register #(.width(5)) EX_MEM_RegDst_2 (
    .D(EX_MEM_RegDst_q), .en(1'b1), .Q(mipsprogramrom_1_p7), .clk(clock_1_out));  // open: clr
  Register #(.width(1)) EX_MEM_Memory_2 (
    .D(EX_MEM_Memory_q[2]), .en(1'b1), .Q(EX_MEM_Memory_2_q), .clk(clock_1_out));  // open: clr
  Register #(.width(1)) EX_MEM_RegisterWriting_2 (
    .D(EX_MEM_RegisterWriting_q), .en(1'b1), .Q(mipsprogramrom_1_p6), .clk(clock_1_out));  // open: clr
  Multiplexer #(.width(32)) multiplexer_4 (
    .in0(EX_MEM_Result_2_q), .in1(mips_ram_1_p6), .out(registerfile_1_p1), .sel(EX_MEM_Memory_2_q));

  // Notes on the sheet:
  //   contents of mipsprogramrom_1 (hex, n*v repeats v):
  //   addiu $1, $1, 0x1      # $1 = 0x0001     addiu $2, $2, 0x2      # $2 = 0x0002     slt $3, $1, $2
  //   # $3 = 1     slt $3, $2, $1         # $3 = 0     slti $3, $1, 0x1       # $3 = 1     slti $3, $1,
  //   0x42      # $3 = 0     or $3, $1, $2          # $3 = 0x3     and $3, $1, $2         # $3 = 0     ori
  //   $3, $1, 0x7        # $3 = 0x7     andi $3, $1, 0x7       # $3 = 0x1     sw $3, 0($0)     lw $5,
  //   0($0)     beq $1, $3, LOL
endmodule

module Control2 (
  input  [5:0] Instruction,
  output SignedIMM,
  output [2:0] Alu,
  output [1:0] Branching,
  output [2:0] Memory,
  output [1:0] RegisterWriting
);
endmodule
